# Fritzing sketch Esquemas de los componetes (saved by Fritzing 0.9.3b)
circuit board: 8.46667cm x 5.64444cm

parts:
  U1 = ESP32S-HiLetgo [part_number=ESP32S-HiLetgo]
  PIR1 = PIR sensor
  J1 = Basic Servo

nets:
  N1: U1.GPIO26, PIR1.SIG
  N2: U1.GPIO27, J1.pulse
  GND: U1.GND, PIR1.GND
  VIN: U1.VIN, PIR1.VDD, J1.vcc

custom parts:
  ESP32S-HiLetgo: HiLetgo ESP-WROOM-32 ESP32 ESP-32S Development Board 2.4GHz Dual-Mode WiFi + Bluetooth Dual Cores Microcontroller The ESP32 integrated with Antenna switches, RF Balun, power amplifiers, low-noise amplifiers, filters, and management modules, and the entire solution occupies the least area of PCB. 2.4 GHz Wi-Fi plus Bluetooth dual-mode chip, with TSMC Ultra-low power consumption 40nm technology,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
